# Fritzing sketch fish-feeder (saved by Fritzing 0.9.3b)

parts:
  ZS-042_RTC1 = ZS-042 RTC Module
  Display1 = LCD screen 16x2 IIC [part_number=101290]
  Part1 = Arduino Uno (Rev3) - ICSP
  J1 = Basic Servo

nets:
  GND: ZS-042_RTC1.GND, Display1.GND, Part1.GND, J1.gnd
  VCC: ZS-042_RTC1.VCC, J1.vcc
  N1: ZS-042_RTC1.SDA, Display1.SDA, Part1.A4/SDA
  N2: ZS-042_RTC1.SCL, Display1.SCL, Part1.A5/SCL
  VCC_2: Display1.VCC, Part1.5V
  N3: Part1.D3_PWM, J1.pulse

custom parts:
  LCD screen 16x2 IIC: LCD screen with HD44780 controller enables showing text, symbols, value or anything else that comes from Croduino/Arduino. It is capable of showing 16 symbols in two lines and therefore can be used in many projects that need to send clearly visible and legible output information.. • Color of symbols: White • Backlight: Blue • Dimensions: 80 x 36 x 12 mm • Screen dimensions: 64.5 x 16 mm •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
